// Logisim project ls32.circ as structural Verilog: 1 circuit, main circuit main
module main (
  input  A,
  input  B,
  input  C,
  output SUM,
  output out_5
);

  wire _1_out, _2_out, _3_out, _4_out, _5_out, _6_out, _7_out;

  nand _1 (_1_out, A, B);
  nand _2 (_2_out, A, _1_out);
  nand _3 (_3_out, _1_out, A);
  nand _4 (_4_out, _2_out, _3_out);
  nand _5 (_5_out, _4_out, C);
  nand _6 (_6_out, _4_out, _5_out);
  // NAND_Gate _7 has open pins: out=_7_out
  nand _8 (SUM, _6_out, _7_out);
  nand _9 (out_5, _5_out, _1_out);

  // Notes on the sheet:
  //   CARRY
endmodule
