// Logisim project ls33.circ as structural Verilog: 1 circuit, main circuit main
module main (
  input  A,
  input  B,
  input  C,
  output CARRY,
  output SUM
);

  wire nor_1_out, nor_2_out, nor_3_out, nor_4_out, nor_5_out, nor_6_out, nor_7_out;

  nor nor_1 (nor_1_out, A, B);
  nor nor_2 (nor_2_out, nor_1_out, B);
  nor nor_3 (nor_3_out, A, nor_1_out);
  nor nor_4 (nor_4_out, nor_3_out, nor_2_out);
  nor nor_5 (nor_5_out, nor_4_out, C);
  nor nor_6 (nor_6_out, nor_4_out, nor_5_out);
  nor nor_7 (nor_7_out, nor_5_out, C);
  nor nor_8 (CARRY, nor_1_out, nor_5_out);
  nor nor_9 (SUM, nor_6_out, nor_7_out);
endmodule
